# Fritzing sketch IR (saved by Fritzing 0.9.0b)

parts:
  IR = Arduino Uno (Rev3)
  IR1 = TSOP312.., 314.. [package=THT]
  J1 = Basic Servo

nets:
  N1: IR.D10_PWM/SS, J1.pulse
  N2: IR.D11_PWM/MOSI, IR1.Data
  GND: IR.GND, IR1.GND, J1.gnd
  N3: IR.3V3, IR1.Vs
  5V: IR.5V, J1.vcc
